// Logisim project exercício_proposto.circ as structural Verilog: 1 circuit, main circuit main
module main (
  input  Reset,
  input  [7:0] Input0,
  input  En_0,
  input  [7:0] Input1,
  input  En_1,
  input  OP
);

  wire Clock_out, FF_OP_1_q, FF_OP_2_q;
  wire [7:0] adder_1_out, FF_1_q, FF_2_q, FF_3_q, FF_4_q, multiplexer_1_out, multiplexer_2_out,
       multiplexer_3_out, subtractor_1_out;

  Clock Clock (.out(Clock_out));
  Multiplexer #(.width(8), .enable("false")) multiplexer_1 (
    .in0(FF_1_q), .in1(Input0), .out(multiplexer_1_out), .sel(En_0));
  Multiplexer #(.width(8), .enable("false")) multiplexer_2 (
    .in0(FF_2_q), .in1(Input1), .out(multiplexer_2_out), .sel(En_1));
  Register FF_1 (.D(multiplexer_1_out), .Q(FF_1_q), .clk(Clock_out), .clr(Reset));  // open: en
  Register FF_2 (.D(multiplexer_2_out), .Q(FF_2_q), .clk(Clock_out), .clr(Reset));  // open: en
  Register #(.width(1)) FF_OP_1 (.D(OP), .Q(FF_OP_1_q), .clk(Clock_out), .clr(Reset));  // open: en
  Adder adder_1 (.a(FF_1_q), .b(FF_2_q), .out(adder_1_out));  // open: cin, cout
  Subtractor subtractor_1 (.a(FF_1_q), .b(FF_2_q), .out(subtractor_1_out));  // open: bin, bout
  Register FF_3 (.D(adder_1_out), .Q(FF_3_q), .clk(Clock_out), .clr(Reset));  // open: en
  Register FF_4 (.D(subtractor_1_out), .Q(FF_4_q), .clk(Clock_out), .clr(Reset));  // open: en
  Register #(.width(1)) FF_OP_2 (.D(FF_OP_1_q), .Q(FF_OP_2_q), .clk(Clock_out), .clr(Reset));  // open: en
  Multiplexer #(.width(8), .enable("false")) multiplexer_3 (
    .in0(FF_3_q), .in1(FF_4_q), .out(multiplexer_3_out), .sel(FF_OP_2_q));
  Register OutPut1 (.D(multiplexer_3_out), .clk(Clock_out), .clr(Reset));  // open: en, Q
endmodule
