// Logisim project circuito3.circ as structural Verilog: 1 circuit, main circuit main
module main (
  input  reset,
  input  [7:0] Input0,
  input  [7:0] Input1,
  input  op_0,
  input  op_1
);

  wire clock_out, FF_0_Op_0_q, FF_0_Op_1_q, FF_1_Op_0_q, FF_1_Op_1_q;
  wire [7:0] adder_1_out, adder_2_out, FF_0_q, FF_1_q, FF_2_q, FF_3_q, multiplexer_1_out, multiplexer_2_out,
       subtractor_1_out;

  Clock clock (.out(clock_out));
  Register FF_0 (.D(Input0), .Q(FF_0_q), .clk(clock_out), .clr(reset));  // open: en
  Register FF_1 (.D(Input1), .Q(FF_1_q), .clk(clock_out), .clr(reset));  // open: en
  Register #(.width(1)) FF_0_Op_0 (.D(op_0), .Q(FF_0_Op_0_q), .clk(clock_out), .clr(reset));  // open: en
  Register #(.width(1)) FF_0_Op_1 (.D(op_1), .Q(FF_0_Op_1_q), .clk(clock_out), .clr(reset));  // open: en
  Subtractor subtractor_1 (.a(FF_0_q), .b(FF_1_q), .out(subtractor_1_out));  // open: bin, bout
  Adder adder_1 (.a(FF_0_q), .b(FF_1_q), .out(adder_1_out));  // open: cin, cout
  Register FF_2 (.D(subtractor_1_out), .Q(FF_2_q), .clk(clock_out), .clr(reset));  // open: en
  Register FF_3 (.D(adder_1_out), .Q(FF_3_q), .clk(clock_out), .clr(reset));  // open: en
  Register #(.width(1)) FF_1_Op_0 (.D(FF_0_Op_0_q), .Q(FF_1_Op_0_q), .clk(clock_out), .clr(reset));  // open: en
  Register #(.width(1)) FF_1_Op_1 (.D(FF_0_Op_1_q), .Q(FF_1_Op_1_q), .clk(clock_out), .clr(reset));  // open: en
  Multiplexer #(.width(8), .enable("false")) multiplexer_1 (
    .in0(FF_2_q), .in1(FF_3_q), .out(multiplexer_1_out), .sel(FF_1_Op_0_q));
  Multiplexer #(.width(8), .enable("false")) multiplexer_2 (
    .in0(FF_2_q), .in1(FF_3_q), .out(multiplexer_2_out), .sel(FF_1_Op_1_q));
  Adder adder_2 (.a(multiplexer_1_out), .b(multiplexer_2_out), .out(adder_2_out));  // open: cin, cout
  Register Output0 (.D(adder_2_out), .clk(clock_out), .clr(reset));  // open: en, Q
endmodule
