// Logisim project mini_processador.circ as structural Verilog: 2 circuits, main circuit main
// MAIN
module main (
  input  [3:0] A,
  input  [3:0] B,
  input  [1:0] S,
  output [3:0] Out,
  output Equal
);

  wire [3:0] adder_1_out, multiplier_1_out, subtractor_1_out;

  Adder #(.width(4)) adder_1 (.a(A), .b(B), .out(adder_1_out));  // open: cin, cout
  Subtractor #(.width(4)) subtractor_1 (.a(A), .b(B), .out(subtractor_1_out));  // open: bin, bout
  Multiplier #(.width(4)) multiplier_1 (.a(A), .b(B), .out(multiplier_1_out));  // open: cin, cout
  Comparator #(.width(4)) comparator_1 (.a(A), .b(B), .eq(Equal));  // open: gt, lt
  Multiplexer #(.select(2), .width(4), .enable("false")) multiplexer_1 (
    .in0({3'b000, Equal}), .in1(adder_1_out), .in2(subtractor_1_out), .in3(multiplier_1_out), .out(Out),
    .sel(S));
endmodule

module ULA3 (
  output LDA,
  output ADD,
  output SUB,
  output MUL,
  output BEQ,
  output BNE,
  output JMP
);

  wire and_1_out, and_2_out, and_3_out, and_4_out, and_5_out, clock_1_out, main_1_equal, not_1_out,
       not_2_out, not_3_out, not_4_out, not_5_out, not_6_out, or_1_out;
  wire [1:0] ram_1_data;
  wire [3:0] counter_1_q, main_1_out, multiplexer_1_out, R0_q, R1_q;
  wire [7:0] ram_1_data_2;

  not not_1 (not_1_out, or_1_out);
  Clock clock_1 (.out(clock_1_out));
  Counter #(.width(4), .max('hf)) counter_1 (
    .load(or_1_out), .D(ram_1_data_2[3:0]), .count(not_1_out), .Q(counter_1_q), .clk(clock_1_out));  // open: carry, clr
  main main_1 (.A(R0_q), .B(R1_q), .S(ram_1_data), .Out(main_1_out), .Equal(main_1_equal));
  RAM #(.addrWidth(4)) ram_1 (
    .addr(counter_1_q), .data({ram_1_data_2[7], ram_1_data, ram_1_data_2[4:0]}));  // open: sel, clk, ld, clr
  Multiplexer #(.width(4), .enable("false")) multiplexer_1 (
    .in0(main_1_out), .in1(ram_1_data_2[3:0]), .out(multiplexer_1_out), .sel(LDA));
  Register #(.width(4)) R0 (.D(multiplexer_1_out), .en(and_4_out), .Q(R0_q), .clk(clock_1_out));  // open: clr
  Register #(.width(4)) R1 (.D(multiplexer_1_out), .en(and_5_out), .Q(R1_q), .clk(clock_1_out));  // open: clr
  Decoder #(.select(3), .enable("false")) decoder_1 (
    .out0(LDA), .out1(ADD), .out2(SUB), .out3(MUL), .out4(BEQ), .out5(BNE), .out6(JMP),
    .sel({ram_1_data_2[7], ram_1_data}));  // open: out7
  not not_2 (not_2_out, ram_1_data_2[4]);
  and and_1 (and_1_out, BEQ, main_1_equal);
  not not_3 (not_3_out, main_1_equal);
  and and_2 (and_2_out, BNE, not_3_out);
  or or_1 (or_1_out, JMP, and_1_out, and_2_out);
  not not_4 (not_4_out, BEQ);
  not not_5 (not_5_out, BNE);
  and and_3 (and_3_out, not_4_out, not_5_out, not_6_out);
  not not_6 (not_6_out, JMP);
  and and_4 (and_4_out, and_3_out, not_2_out);
  and and_5 (and_5_out, and_3_out, ram_1_data_2[4]);
endmodule
