// Logisim project arch_reg.circ as structural Verilog: 1 circuit, main circuit main
module main (
  input  reset,
  input  [7:0] In1,
  input  [7:0] In2,
  input  [7:0] In3,
  output [7:0] out_5,
  output [7:0] out_6,
  output [7:0] Out1
);

  wire clock_out;
  wire [7:0] register_1_q, register_2_q, register_3_q;

  Clock clock (.out(clock_out));
  Register register_1 (.D(In1), .Q(register_1_q), .clk(clock_out), .clr(reset));  // open: en
  Register register_2 (.D(In2), .Q(register_2_q), .clk(clock_out), .clr(reset));  // open: en
  Register register_3 (.D(In3), .Q(register_3_q), .clk(clock_out), .clr(reset));  // open: en
  Adder adder_1 (.a(register_1_q), .b(register_2_q), .out(out_5));  // open: cin, cout
  Subtractor subtractor_1 (.a(out_5), .b(register_3_q), .out(out_6));  // open: bin, bout
  Register register_4 (.D(out_6), .Q(Out1), .clk(clock_out), .clr(reset));  // open: en
endmodule
