// Logisim project arch_reg_pipe.circ as structural Verilog: 1 circuit, main circuit main
module main (
  input  reset,
  input  [7:0] In1,
  input  [7:0] In2,
  input  [7:0] In3,
  output [7:0] out_5,
  output [7:0] out_6,
  output [7:0] Out1
);

  wire clock_out;
  wire [7:0] A_q, B_q, C_q, D_q, E_q;

  Clock clock (.out(clock_out));
  Register A (.D(In1), .Q(A_q), .clk(clock_out), .clr(reset));  // open: en
  Register B (.D(In2), .Q(B_q), .clk(clock_out), .clr(reset));  // open: en
  Register C (.D(In3), .Q(C_q), .clk(clock_out), .clr(reset));  // open: en
  Adder adder_1 (.a(A_q), .b(B_q), .out(out_5));  // open: cin, cout
  Register D (.D(out_5), .Q(D_q), .clk(clock_out));  // open: en, clr
  Register E (.D(C_q), .Q(E_q), .clk(clock_out));  // open: en, clr
  Subtractor subtractor_1 (.a(D_q), .b(E_q), .out(out_6));  // open: bin, bout
  Register F (.D(out_6), .Q(Out1), .clk(clock_out), .clr(reset));  // open: en
endmodule
