// Logisim project ULA.circ as structural Verilog: 1 circuit, main circuit main
module main (
  input  [7:0] in1,
  input  [7:0] in2,
  input  [1:0] Sel,
  output [7:0] out_4,
  output [7:0] out_5,
  output [7:0] out1,
  output [7:0] out_7
);

  Adder adder_1 (.a(in1), .b(in2), .out(out_4));  // open: cin, cout
  Subtractor subtractor_1 (.a(in1), .b(in2), .out(out_5));  // open: bin, bout
  Multiplier multiplier_1 (.a(in1), .b(in2), .out(out_7));  // open: cin, cout
  Multiplexer #(.select(2), .width(8), .enable("false")) multiplexer_1 (
    .in0(out_4), .in1(out_5), .in2(out_7), .out(out1), .sel(Sel));  // open: in3
endmodule
